# Fritzing sketch schematics-slider (saved by Fritzing 1.0.4)
breadboards: 1

parts:
  S1 = Pushbutton [package="[THT]"]
  R1 = Rotary Potentiometer (Small) [maximum_resistance=10kΩ knob_status=50% power=0.5W package=THT]
  S3 = Pushbutton [package="[THT]"]
  Composant1 = Arduino Uno (Rev3)  # not connected
  HC-SR04_Sensor_1 = HC-SR04 Ultrasonic Distance Sensor
  HC-SR04_Sensor_2 = HC-SR04 Ultrasonic Distance Sensor
  Composant2 = Adafruit Motor/Stepper/Servo Shield [part_number="Adafruit #1438"]
  M1 = Stepper Motor - Bipolar

nets:
  N1: S1.Pin_3, S1.Pin_4, Composant2.AD0
  GND: R1.leg1, S3.Pin_1, S3.Pin_2, HC-SR04_Sensor_1.GND, HC-SR04_Sensor_2.GND, Composant2.GND
  VCC: R1.leg2, HC-SR04_Sensor_1.VCC, HC-SR04_Sensor_2.VCC, Composant2.+5V
  N2: S3.Pin_3, S3.Pin_4, Composant2.D2
  N3: HC-SR04_Sensor_1.TRIG, Composant2.D5
  N4: HC-SR04_Sensor_1.ECHO, Composant2.D6
  N5: HC-SR04_Sensor_2.TRIG, Composant2.D3
  N6: HC-SR04_Sensor_2.ECHO, Composant2.D4
  N7: Composant2.M3A, M1.B
  N8: Composant2.M3B, M1.D
  N9: Composant2.M4B, M1.C
  N10: Composant2.M4A, M1.A

custom parts:
  Adafruit Motor/Stepper/Servo Shield: The original Adafruit Motorshield kit is one of our most beloved kits, which is why we decided to make something even better. We have upgraded the shield kit to make the bestest, easiest way to drive DC and Stepper motors. This shield will make quick work of your next robotics project! We kept the ability to drive up to 4 DC motors or 2 stepper motors, but added many improvements: Instead of a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
